# Fritzing sketch HC-12 remote control (saved by Fritzing 0.9.6b)
breadboards: 1

parts:
  HC-12 = HC-12 Module
  Espessif_Serial_Wifi_Modul_1 = ESP8266 ESP01 [part_number=ESP8266 package=THT]
  Antenna1 = HC-12 Antenna
  3_3V = LIPO-2000mAh [package=lipo-2000]
  0_01uf = Capacitor [package=cap-pth-small2]
  C1 = Electrolytic Capacitor [capacitance=1000μF voltage=35V package="1010 [SMD, electrolytic]"]
  IC1 = Voltage Regulator [package=to-92]

nets:
  N1: HC-12.TXD, Espessif_Serial_Wifi_Modul_1.RXD
  N2: HC-12.RXD, Espessif_Serial_Wifi_Modul_1.TXD
  GND: HC-12.GND, Espessif_Serial_Wifi_Modul_1.GND, 3_3V.-, 0_01uf.2, C1.-, IC1.GND
  N3: HC-12.VCC, 3_3V.+, 0_01uf.1, C1.+, IC1.IN
  N4: HC-12.ANT, Antenna1.ANT
  N5: Espessif_Serial_Wifi_Modul_1.VCC, IC1.OUT

custom parts:
  HC-12 Module: HC-12 433Mhz Module
  ESP8266 ESP01: Generic WiFi Module based on the ESP8266 with onboard PCB antenna and UART communications
  HC-12 Antenna: Antenna for HC-12 433Mhz Module
