# Fritzing sketch Repeater Control (saved by Fritzing 0.9.6b)
stripboards: 1

parts:
  NTE1904 = Voltage Regulator - 3.3V [package="TO220 [THT]"]
  L7805 = Voltage Regulator - 5V [package="DPak [SMD]"]
  OLED = Grove OLED 128x96
  S1 = Round Pushbutton
  L7809 = Voltage Regulator [package=to220-adj]
  100uf = Capacitor Polarized [package=cpol-radial-100uf-25v]
  C2 = Capacitor Polarized [package=cpol-radial-100uf-25v]
  100uf_2 = Capacitor Polarized [package=cpol-radial-100uf-25v]
  C4 = Capacitor Polarized [package=cpol-radial-10uf-25v]
  10uf = Capacitor Polarized [package=cpol-radial-10uf-25v]
  10uf_2 = Capacitor Polarized [package=cpol-radial-10uf-25v]
  RHT1 = Humidity and Temperature Sensor RHT03
  C7 = Capacitor [package=cap-pth-small-kit]
  022uf = Capacitor [package=cap-pth-small-kit]
  0_22uf = Capacitor [package=cap-pth-small-kit]
  9V = Header 3 [package=screwterminal-3.5mm-3_lock.007s]
  Arduino_Mega_2560 = Arduino Mega 2560 (Rev3)
  12V = Header 3 [package=screwterminal-3.5mm-3_lock.007s]
  5V = Header 3 [package=screwterminal-3.5mm-3_lock.007s]
  3_3V = Header 3 [package=screwterminal-3.5mm-3_lock.007s]
  12_V = Battery block 9V
  Relay = G3VM-61E1 [package=g3vm-61e1]
  HC-1 = HC-12 Module
  Antenna1 = HC-12 Antenna
  microSD1 = MicroSD Card Module
  R1 = Resistor [tolerance=±5% resistance=1k package="1206 [SMD]"]
  R2 = Resistor [tolerance=±5% resistance=1M package="0402 [SMD]"]
  RTC1 = ZS-042 RTC Module

nets:
  N1: NTE1904.input_voltage, NTE1904.GND, NTE1904.output_voltage, C7.1, C7.2
  N2: L7805.input_voltage, L7805.GND, 100uf_2.+, 100uf_2.-, 10uf.-, 022uf.1
  N3: L7805.output_voltage, 10uf.+, 022uf.2
  N4: OLED.VCC, 5V.2
  N5: S1.leg1, L7809.ADJ, L7809.IN, 100uf.+, 100uf.-, 10uf_2.-, RHT1.GND_1, RHT1.GND_2, 0_22uf.1, 9V.1, 9V.3, Arduino_Mega_2560.GND, 12V.1, 12V.3, 12_V.-, Relay.P$4, R1.Pin_1
  N6: L7809.OUT, 10uf_2.+, 0_22uf.2
  N7: C2.+, C2.-, 3_3V.1, 3_3V.3, HC-1.GND
  N8: C4.+, C4.-
  VCC: RHT1.Vcc, Arduino_Mega_2560.3V3
  N9: RHT1.Data-signal, Arduino_Mega_2560.A1
  N10: 9V.2, Arduino_Mega_2560.VIN
  N11: Arduino_Mega_2560.A3, R2.Pin_1
  N12: Arduino_Mega_2560.D21/SCL, RTC1.SCL
  N13: Arduino_Mega_2560.D20/SDA, RTC1.SDA
  N14: Arduino_Mega_2560.D19/RX1, HC-1.TXD
  N15: Arduino_Mega_2560.D18/TX1, HC-1.RXD
  N16: Arduino_Mega_2560.D12_PWM, Relay.P$2
  N17: Arduino_Mega_2560.D4_PWM, Arduino_Mega_2560.D53
  N18: Arduino_Mega_2560.D50, microSD1.MOSI
  N19: Arduino_Mega_2560.D51, microSD1.MISO
  N20: Arduino_Mega_2560.D52, microSD1.SCK
  N21: 5V.1, Relay.P$1
  N22: 5V.3, Relay.P$3
  N23: 3_3V.2, HC-1.VCC
  N24: HC-1.ANT, Antenna1.ANT

custom parts:
  HC-12 Module: HC-12 433Mhz Module
  HC-12 Antenna: Antenna for HC-12 433Mhz Module
